# Fritzing sketch FritzingCarShkeme (saved by Fritzing 1.0.1rc)

parts:
  Част1 = ESP12E Motor Shield
  Mod1 = Amica NodeMCU DEVKIT 1.0
  M1 = gear-motor
  M2 = gear-motor
  M3 = gear-motor
  M4 = gear-motor
  BATT1 = 4xAA Switchable Battery Pack w/Bare Wire

nets:
  N1: Част1.3V3, Mod1.pin1, Mod1.pin_10, Mod1.pin_26
  N2: Част1.G, Mod1.pin2, Mod1.pin_9, Mod1.pin_25, Mod1.pin_29
  N3: Част1.SD0, Mod1.pin_23
  N4: Част1.CMD, Mod1.pin_22
  N5: Част1.SD1, Mod1.pin_21
  N6: Част1.RSV#40, Mod1.pin_18
  N7: Част1.VIN#43, Mod1.pin_30
  N8: Част1.RST, Mod1.pin_28
  N9: Част1.EN, Mod1.pin_27
  N10: Част1.CLK, Mod1.pin_24
  N11: Част1.SD2, Mod1.pin_20
  N12: Част1.SD3, Mod1.pin_19
  N13: Част1.RSV#52, Mod1.pin_17
  N14: Част1.AD0, Mod1.pin_16
  N15: Част1.TX, Mod1.pin3
  N16: Част1.RX, Mod1.pin4
  N17: Част1.D8, Mod1.pin5
  N18: Част1.D7, Mod1.pin6
  N19: Част1.D6, Mod1.pin7
  N20: Част1.D5, Mod1.pin8
  N21: Част1.CB, Mod1.pin_11
  N22: Част1.DA, Mod1.pin_12
  N23: Част1.PWMB, Mod1.pin_13
  N24: Част1.PWMA, Mod1.pin_14
  N25: Част1.D0, Mod1.pin_15
  N26: Част1.VIN#74, Част1.VM
  N27: Част1.A-, M1.pin_2, M2.pin_2
  N28: Част1.A+, M1.pin_1, M2.pin_1
  N29: Част1.B-, M3.pin_2, M4.pin_2
  N30: Част1.B+, M3.pin_1, M4.pin_1
  N31: Част1.VIN#102, BATT1.POS
  N32: Част1.GND, BATT1.NEG

custom parts:
  ESP12E Motor Shield: ESP8266 WiFi Motor Drive Expansion Board For NodeMCU ESP-12E
  4xAA Switchable Battery Pack w/Bare Wire: 4xAA Switchable Battery Pack with Bare Wire connection
