# Fritzing sketch shemata (saved by Fritzing 1.0.1rc)
breadboards: 1

parts:
  IC1 = L293D [package=THT]
  U1 = NodeMCU V1.0
  M1 = gear-motor
  M2 = gear-motor
  M3 = gear-motor
  M4 = gear-motor

nets:
  N1: IC1.Enable_1, IC1.Enable_2, IC1.+V, U1.3V3
  N2: IC1.In_1, U1.D2
  N3: IC1.Out_1_(_Controlled_by_Enable_1_), M3.pin_2, M4.pin_2
  N4: IC1.0V, U1.GND
  N5: IC1.Out_2_(_Controlled_by_Enable_1_), M3.pin_1, M4.pin_1
  N6: IC1.In_2, U1.D3
  6V: IC1.+Vmotor
  N7: IC1.In_3, U1.D5
  N8: IC1.Out_3_(_Controlled_by_Enable_2_), M1.pin_1, M2.pin_1
  N9: IC1.Out_4_(_Controlled_by_Enable_2_), M1.pin_2, M2.pin_2
  N10: IC1.In_4, U1.D6

custom parts:
  NodeMCU V1.0: ESP8266 based NodeMCU
